// Logisim project 1.circ as structural Verilog: 1 circuit, main circuit main
module main (
  input  [15:0] GB2312,
  input  [15:0] GB2312_2
);

  wire adder_1_cout;
  wire [15:0] adder_1_out;

  Adder #(.width(16)) adder_1 (.a(GB2312), .b(GB2312_2), .out(adder_1_out), .cout(adder_1_cout));  // open: cin
  // Probe on adder_1_cout
  // Probe on adder_1_out
endmodule
